// Logisim project spi2parallel2spi.circ as structural Verilog: 3 circuits, main circuit main
module main (
  input  in_1,
  input  in_2,
  input  in_3,
  input  in_4,
  input  in_5
);

  wire n74164_1_pin3, n74164_1_pin4, n74164_1_pin5, n74164_1_pin6, n74164_1_pin10, n74164_1_pin11,
       n74164_1_pin12, n74164_1_pin13, n74164_2_pin3, n74164_2_pin4, n74164_2_pin5, n74164_2_pin6,
       n74164_2_pin10, n74164_2_pin11, n74164_2_pin12, n74164_2_pin13, undriven, undriven_2, undriven_3,
       undriven_4, undriven_5, undriven_6, undriven_7, undriven_8, undriven_9, undriven_10;

  LED led_1 (.in(n74164_1_pin3));
  LED led_2 (.in(n74164_1_pin4));
  LED led_3 (.in(n74164_1_pin5));
  LED led_4 (.in(n74164_1_pin6));
  LED led_5 (.in(n74164_1_pin10));
  LED led_6 (.in(n74164_1_pin11));
  _74164 u_74164_1 (
    .pin1(in_2), .pin2(in_2), .pin3(n74164_1_pin3), .pin4(n74164_1_pin4), .pin5(n74164_1_pin5),
    .pin6(n74164_1_pin6), .pin13(n74164_1_pin13), .pin12(n74164_1_pin12), .pin11(n74164_1_pin11),
    .pin10(n74164_1_pin10), .pin9(in_4), .pin8(in_1));
  LED led_7 (.in(n74164_1_pin12));
  LED led_8 (.in(n74164_1_pin13));
  PSRAM psram_1 (
    .in_1(undriven_2), .in_7(undriven_10), .in_2(undriven), .in_8(undriven_3));  // open: in_3, in_5, in_4, in_6
  PSRAM psram_2 (
    .in_1(undriven_4), .in_7(undriven_10), .in_2(undriven), .in_8(undriven_5));  // open: in_3, in_5, in_4, in_6
  PSRAM psram_3 (
    .in_1(undriven_6), .in_7(undriven_10), .in_2(undriven), .in_8(undriven_7));  // open: in_3, in_5, in_4, in_6
  PSRAM psram_4 (
    .in_1(undriven_8), .in_7(undriven_10), .in_2(undriven), .in_8(undriven_9));  // open: in_3, in_5, in_4, in_6
  LED led_9 (.in(n74164_2_pin3));
  LED led_10 (.in(n74164_2_pin4));
  LED led_11 (.in(n74164_2_pin5));
  LED led_12 (.in(n74164_2_pin6));
  LED led_13 (.in(n74164_2_pin10));
  LED led_14 (.in(n74164_2_pin11));
  _74164 u_74164_2 (
    .pin1(in_2), .pin2(in_2), .pin3(n74164_2_pin3), .pin4(n74164_2_pin4), .pin5(n74164_2_pin5),
    .pin6(n74164_2_pin6), .pin13(n74164_2_pin13), .pin12(n74164_2_pin12), .pin11(n74164_2_pin11),
    .pin10(n74164_2_pin10), .pin9(in_4), .pin8(in_1));
  LED led_15 (.in(n74164_2_pin12));
  LED led_16 (.in(n74164_2_pin13));
endmodule

module Inside74HC164 (
  input  in_1,
  input  in_2,
  input  in_3,
  input  in_4
);

  wire and_1_out, d_ff_1_q, d_ff_2_q, d_ff_3_q, d_ff_4_q, d_ff_5_q, d_ff_6_q, d_ff_7_q, d_ff_8_q;

  and and_1 (and_1_out, in_1, in_2);
  D_Flip_Flop d_ff_1 (.D(and_1_out), .clk(in_3), .Q(d_ff_1_q), .reset(in_4));  // open: Qn, preset
  D_Flip_Flop d_ff_2 (.D(d_ff_1_q), .clk(in_3), .Q(d_ff_2_q), .reset(in_4));  // open: Qn, preset
  LED led_1 (.in(d_ff_1_q));
  D_Flip_Flop d_ff_3 (.D(d_ff_2_q), .clk(in_3), .Q(d_ff_3_q), .reset(in_4));  // open: Qn, preset
  LED led_2 (.in(d_ff_2_q));
  D_Flip_Flop d_ff_4 (.D(d_ff_3_q), .clk(in_3), .Q(d_ff_4_q), .reset(in_4));  // open: Qn, preset
  LED led_3 (.in(d_ff_3_q));
  D_Flip_Flop d_ff_5 (.D(d_ff_4_q), .clk(in_3), .Q(d_ff_5_q), .reset(in_4));  // open: Qn, preset
  LED led_4 (.in(d_ff_4_q));
  LED led_5 (.in(d_ff_5_q));
  D_Flip_Flop d_ff_6 (.D(d_ff_5_q), .clk(in_3), .Q(d_ff_6_q), .reset(in_4));  // open: Qn, preset
  LED led_6 (.in(d_ff_6_q));
  D_Flip_Flop d_ff_7 (.D(d_ff_6_q), .clk(in_3), .Q(d_ff_7_q), .reset(in_4));  // open: Qn, preset
  LED led_7 (.in(d_ff_7_q));
  D_Flip_Flop d_ff_8 (.D(d_ff_7_q), .clk(in_3), .Q(d_ff_8_q), .reset(in_4));  // open: Qn, preset
  LED led_8 (.in(d_ff_8_q));
endmodule

module PSRAM (
  input  in_1,
  input  in_2,
  input  in_3,
  input  in_4,
  input  in_5,
  input  in_6,
  input  in_7,
  input  in_8
);
endmodule
